# Fritzing sketch auralink_pcb (saved by Fritzing 1.0.5)
circuit board: 17.4146cm x 8.73494cm
breadboards: 2

parts:
  100K = Trimmer Potentiometer [maximum_resistance=10kΩ knob_status=50% power=0.5W package=THT]
  SPI_TFT_DISPLAY = female pin header, 8 pins [form="♀ (female)"]
  BH1750 = female pin header, 5 pins [form="♀ (female)"]
  BME280 = female pin header, 4 pins [form="♀ (female)"]
  RTC = female pin header, 6 pins [form="♀ (female)"]
  MQ135 = female pin header, 4 pins [form="♀ (female)"]
  UV = female pin header, 3 pins [form="♀ (female)"]
  TOUCH_L = female pin header, 3 pins [form="♀ (female)"]
  TOUCH_R = female pin header, 3 pins [form="♀ (female)"]
  BAT_LEVEL = female pin header, 3 pins [form="♀ (female)"]
  CHARGER = female pin header, 3 pins [form="♀ (female)"]
  R = Resistor [tolerance=±5% resistance=220 power=0.25W package=THT]
  R_2 = Resistor [tolerance=±5% resistance=220 power=0.25W package=THT]
  R_3 = Resistor [tolerance=±5% resistance=220 power=0.25W package=THT]
  2R = Resistor [tolerance=±5% resistance=220 power=0.25W package=THT]
  C1 = Electrolytic Capacitor [capacitance=10μF voltage=35V package="100 mil [THT, electrolytic]"]
  C2 = Electrolytic Capacitor [capacitance=10μF voltage=35V package="100 mil [THT, electrolytic]"]
  RST = female pin header, 2 pins [form="♀ (female)"]
  C4 = Ceramic Capacitor [capacitance="100 nF" voltage=35V package="100 mil [THT, multilayer]"]
  R_4 = Resistor [tolerance=±5% resistance=220 power=0.25W package=THT]
  2R_2 = Resistor [tolerance=±5% resistance=220 power=0.25W package=THT]
  ESP32S3-DevKitC-1 = Werner Rothschopf (modified to ESP32-S3-DevKitC dual USB by vanepp Aug 2024)
  C5 = Ceramic Capacitor [capacitance="100 nF" voltage=35V package="100 mil [THT, multilayer]"]
  P-MOSFET = Basic FET P-Channel [package="TO220 [THT]"]
  R_5 = Resistor [tolerance=±5% resistance=220 power=0.25W package=THT]
  D1 = Schottky Diode [part_number=1N5817 package="300 mil [THT]"]
  Boost_Convertor = Boost Convertor [part_number=XL6009E1 package=THT]
  TP4056 = TP4056 [part_number=TP4056]
  SW = female pin header, 2 pins [form="♀ (female)"]
  Buck_Convertor = Buck Convertor [part_number=LM2596 package=THT]
  3_3V = female pin header, 4 pins [form="♀ (female)"]
  GND = female pin header, 4 pins [form="♀ (female)"]
  5V = female pin header, 4 pins [form="♀ (female)"]
  100K_2 = Resistor [tolerance=±5% resistance=220 power=0.25W package=THT]
  100K_3 = Resistor [tolerance=±5% resistance=220 power=0.25W package=THT]
  IIC1 = female pin header, 2 pins [form="♀ (female)"]
  IIC2 = female pin header, 2 pins [form="♀ (female)"]
  DFPlayer = DFRobot DFPlayer Mini [part_number=DFR0299]
  SPK = female pin header, 2 pins [form="♀ (female)"]
  C6 = Ceramic Capacitor [capacitance="100 nF" voltage=35V package="100 mil [THT, multilayer]"]

nets (from the pcb view):
  N1: 100K.leg1, 100K.wiper, SPI_TFT_DISPLAY.pin8, BH1750.pin1, BH1750.pin5, BME280.pin4, RTC.pin2, UV.pin2, TOUCH_L.pin3, TOUCH_R.pin3, C2.+, Buck_Convertor.Positive_Output, 3_3V.pin1, 3_3V.pin2, 3_3V.pin3, 3_3V.pin4
  N2: 100K.leg2, SPI_TFT_DISPLAY.pin1
  N3: SPI_TFT_DISPLAY.pin2, ESP32S3-DevKitC-1.Pin_20
  N4: SPI_TFT_DISPLAY.pin3, ESP32S3-DevKitC-1.Pin_19
  N5: SPI_TFT_DISPLAY.pin4, ESP32S3-DevKitC-1.Pin_18
  N6: SPI_TFT_DISPLAY.pin5, ESP32S3-DevKitC-1.Pin_17
  N7: SPI_TFT_DISPLAY.pin6, ESP32S3-DevKitC-1.Pin_16
  N8: SPI_TFT_DISPLAY.pin7, BH1750.pin4, BME280.pin3, RTC.pin1, MQ135.pin3, UV.pin3, TOUCH_L.pin1, TOUCH_R.pin1, R_3.Pin_0, 2R.Pin_0, C1.-, C2.-, RST.pin2, C4.0, 2R_2.Pin_0, ESP32S3-DevKitC-1.Pin_22, ESP32S3-DevKitC-1.Pin_44, C5.0, R_5.Pin_0, Boost_Convertor.Negative_Output, Buck_Convertor.Negative_Output, GND.pin1, GND.pin2, GND.pin3, GND.pin4, 100K_2.Pin_0, 100K_3.Pin_0, DFPlayer.GND-2, C6.0
  N9: BH1750.pin2, BME280.pin1, RTC.pin3, ESP32S3-DevKitC-1.Pin_11, IIC1.pin1, IIC2.pin1
  N10: BH1750.pin3, BME280.pin2, RTC.pin4, ESP32S3-DevKitC-1.Pin_10, IIC1.pin2, IIC2.pin2
  N11: MQ135.pin1, R_4.Pin_1
  N12: MQ135.pin4, C1.+, 5V.pin3, 5V.pin4
  N13: UV.pin1, ESP32S3-DevKitC-1.Pin_6
  N14: TOUCH_L.pin2, ESP32S3-DevKitC-1.Pin_9, 100K_3.Pin_1
  N15: TOUCH_R.pin2, ESP32S3-DevKitC-1.Pin_8, 100K_2.Pin_1
  N16: BAT_LEVEL.pin1, BAT_LEVEL.pin2, BAT_LEVEL.pin3, R_2.Pin_0, P-MOSFET.gate, R_5.Pin_1, D1.anode, TP4056.pin1
  N17: CHARGER.pin1, CHARGER.pin2, CHARGER.pin3, R.Pin_0, TP4056.pin4
  N18: R.Pin_1, 2R.Pin_1, C4.1, ESP32S3-DevKitC-1.Pin_5
  N19: R_2.Pin_1, R_3.Pin_1, ESP32S3-DevKitC-1.Pin_4, C6.1
  N20: RST.pin1, ESP32S3-DevKitC-1.Pin_3
  N21: R_4.Pin_0, 2R_2.Pin_1, ESP32S3-DevKitC-1.Pin_12, C5.1
  N22: ESP32S3-DevKitC-1.Pin_1, ESP32S3-DevKitC-1.Pin_2
  N23: ESP32S3-DevKitC-1.Pin_21, SW.pin2, Buck_Convertor.Positive_Input, 5V.pin1, 5V.pin2, DFPlayer.VCC
  N24: ESP32S3-DevKitC-1.Pin_38, DFPlayer.TX
  N25: ESP32S3-DevKitC-1.Pin_39, DFPlayer.RX
  N26: P-MOSFET.drain, Boost_Convertor.Positive_Output
  N27: P-MOSFET.source, D1.cathode, SW.pin1
  N28: Boost_Convertor.Negative_Input, TP4056.pin6, Buck_Convertor.Negative_Input
  N29: Boost_Convertor.Positive_Input, TP4056.pin3
  N30: DFPlayer.SPK_1, SPK.pin1
  N31: DFPlayer.SPK_2, SPK.pin2

custom parts:
  Werner Rothschopf (modified to ESP32-S3-DevKitC dual USB by vanepp Aug 2024): ESP32-S3 ESP32-S3-DevKitC-1 Dual USB development board Pyboard CircuitPython Micropython wifi BLE5.0 ESP32-S3.
  Boost Convertor: DC to DC boost convertor
  TP4056: TP4056 Lithium battery charger / protection module. (this one has the pins on .1 boundaried unlike the original)
  Buck Convertor: DC to DC buck convertor
